// Logisim project FULL SUBTRACTOR.circ as structural Verilog: 1 circuit, main circuit main
module main (
  input  A,
  input  B,
  input  B_in,
  output DIFFERENCE,
  output out_5
);

  wire and_1_out, and_2_out, not_1_out, not_2_out, xor_1_out;

  xor xor_1 (xor_1_out, A, B);
  xor xor_2 (DIFFERENCE, xor_1_out, B_in);
  not not_1 (not_1_out, xor_1_out);
  not not_2 (not_2_out, A);
  and and_1 (and_1_out, not_1_out, B_in);
  and and_2 (and_2_out, not_2_out, B);
  or or_1 (out_5, and_1_out, and_2_out);

  // Notes on the sheet:
  //   FULL SUBTRACTOR
  //   BORROW
endmodule
