// Logisim project HALF ADDER.circ as structural Verilog: 1 circuit, main circuit main
module main (
  input  A,
  input  B,
  output SUM,
  output out_4
);

  xor xor_1 (SUM, A, B);
  and and_1 (out_4, A, B);

  // Notes on the sheet:
  //   HALF ADDER
  //   CARRY
endmodule
