// Logisim project HALF SUBTRACTOR.circ as structural Verilog: 1 circuit, main circuit main
module main (
  input  A,
  input  A_2,
  output out_3,
  output BORROW
);

  wire not_1_out;

  not not_1 (not_1_out, A);
  xor xor_1 (out_3, A, A_2);
  and and_1 (BORROW, not_1_out, A_2);

  // Notes on the sheet:
  //   DIFFERENCE
  //   HALF SUBTRACTOR
endmodule
